# Fritzing sketch IluminateMeFritzingSketchSolder (saved by Fritzing 0.9.3b)

parts:
  Part1 = Adafruit Feather HUZZAH ESP8266 [part_number="Adafruit #2821"]
  Part2 = 12 NeoPixel Ring [part_number=1643]
  BATT1 = LiPoly Battery (1300mAh)  # not connected

nets:
  GND: Part1.GND, Part2.GND
  3.3V: Part1.3.3V, Part2.VDD
  N1: Part1.GPIO13/MOSI, Part2.IN

custom parts:
  Adafruit Feather HUZZAH ESP8266: his is the Adafruit Feather HUZZAH ESP8266 - our take on an 'all-in-one' ESP8266 WiFi development board with built in USB and battery charging. Its an ESP8266 WiFi module with all the extras you need, ready to rock! We have other boards in the Feather family, check'em out here. At the Feather HUZZAH's heart is an ESP8266 WiFi microcontroller clocked at 80 MHz and at 3.3V logic. This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
  12 NeoPixel Ring: 12 ultra bright smart LED NeoPixels are arranged in a circle with 1.5" (37mm) outer diameter. The rings are 'chainable' - connect the output pin of one to the input pin of another. Use only one microcontroller pin to control as many as you can chain together! Each LED is addressable as the driver chip is inside the LED. Each one has ~18mA constant current drive so the color will be very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
  LiPoly Battery (1300mAh): Lithium Ion Polymer Battery (1300mAh)
